# Fritzing sketch CDS (saved by Fritzing 0.9.3b)
breadboards: 1

parts:
  부품1 = Arduino Uno (Rev3)
  R3 = Resistor [tolerance=±5% resistance=220 package=THT]
  R4 = Photocell (LDR) [package=THT]

nets:
  N1: 부품1.A0, R3.Pin_1, R4.pin_0
  N2: 부품1.5V, R3.Pin_0
  N3: 부품1.GND, R4.pin_1
