# Fritzing sketch Display (saved by Fritzing 0.9.3b)
breadboards: 1

parts:
  부품1 = Arduino Uno (Rev3)
  R6 = Resistor [tolerance=±5% resistance=220 package=THT]  # not connected
  U2 = LCD-16X2 [package=lcd-16x2_noholes]  # not connected
  R7 = Rotary Potentiometer (Small) [maximum_resistance=100kΩ package=THT]
  R8 = Resistor [tolerance=±5% resistance=220 package=THT]

nets:
  N1: 부품1.GND, R7.leg1
  N2: 부품1.5V, R7.leg2, R8.Pin_1
