# Fritzing sketch LED_Button (saved by Fritzing 0.9.3b)
breadboards: 1

parts:
  부품1 = Arduino Uno (Rev3)
  LED8 = LED - 5mm [color="Red (633nm)" package="5 mm [THT]"]
  S1 = Pushbutton [package="[THT]"]
  R2 = Resistor [tolerance=±5% resistance=220 package=THT]
  R3 = Resistor [tolerance=±5% resistance=220 package=THT]

nets:
  N1: 부품1.D10_PWM/SS, LED8.anode
  N2: 부품1.GND, R2.Pin_0, R3.Pin_0
  N3: 부품1.D2, S1.Pin_1, S1.Pin_2, R2.Pin_1
  N4: 부품1.5V, S1.Pin_3, S1.Pin_4
  N5: LED8.cathode, R3.Pin_1
