# Fritzing sketch LED_Sensor (saved by Fritzing 0.9.3b)
breadboards: 1

parts:
  부품1 = Arduino Uno (Rev3)
  LED8 = LED - 5mm [color="Red (633nm)" package="5 mm [THT]"]
  R3 = Resistor [tolerance=±5% resistance=220 package=THT]
  부품2 = HC-SR501 Body Sensor Module

nets:
  N1: 부품1.D10_PWM/SS, LED8.anode
  GND: 부품1.GND, R3.Pin_0, 부품2.GND
  N2: 부품1.D2, 부품2.OUT
  5V: 부품1.5V, 부품2.VCC
  N3: LED8.cathode, R3.Pin_1

custom parts:
  HC-SR501 Body Sensor Module: Pyroelectric Infrared PIR Motion Sensor Detector Module
