# Fritzing sketch LED3_bmp180 (saved by Fritzing 0.9.3b)
breadboards: 1

parts:
  Raspberry_Pi_1 = Raspberry Pi 3 [part_number=RPI-3-V1.2]
  LED1 = smd LED [color="Red (633nm)" package="0603 [SMD]"]
  LED2 = smd LED [color="Yellow (595nm)" package="0603 [SMD]"]
  LED3 = smd LED [color="Blue (525nm)" package="0603 [SMD]"]
  R1 = Resistor [tolerance=±5% resistance=220 package=THT]
  R2 = Resistor [tolerance=±5% resistance=220 package=THT]
  R3 = Resistor [tolerance=±5% resistance=220 package=THT]
  Часть2 = BMP180 Breakout (GY-68)

nets:
  3V3: Raspberry_Pi_1.3v3, Часть2.VCC
  N1: Raspberry_Pi_1.GPIO2, Часть2.SDA
  N2: Raspberry_Pi_1.GPIO3, Часть2.SCL
  GND: Raspberry_Pi_1.GND, R1.Pin_0, R2.Pin_0, R3.Pin_0, Часть2.GND
  N3: Raspberry_Pi_1.GPIO17, LED3.anode
  N4: Raspberry_Pi_1.GPIO18, LED1.anode
  N5: Raspberry_Pi_1.GPIO15, LED2.anode
  N6: LED1.cathode, R3.Pin_1
  N7: LED2.cathode, R1.Pin_1
  N8: LED3.cathode, R2.Pin_1

notes:
  LED 3개 연결
  9번 노란색
  10번 파란색
  11번 빨간색

custom parts:
  BMP180 Breakout (GY-68): This is a simple breakout board for the BMP180, a high-precision, low-power barometric pressure sensor made by Bosch Sensortec. The range of measurement is from 300hPa to 1100hPa. The sensor can be supplied with voltage ranging from 1.8V to 3.6V. Operating temperature range is -40 to +85 °C. This particular breakout board (or perhaps the configuration) is produced by Shenzhen Keep Power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
