# Fritzing sketch Sensor_cho_LED (saved by Fritzing 0.9.3b)
breadboards: 1

parts:
  부품1 = Arduino Uno (Rev3)
  hc-sr1 = hc-sr04
  LED1 = LED - 5mm [color="Red (633nm)" package="5 mm [THT]"]
  LED2 = LED - 5mm [color="Yellow (592nm)" package="5 mm [THT]"]
  LED3 = LED - 5mm [color="Green (555nm)" package="5 mm [THT]"]
  R1 = Resistor [tolerance=±5% resistance=220 package=THT]
  R2 = Resistor [tolerance=±5% resistance=220 package=THT]
  R3 = Resistor [tolerance=±5% resistance=220 package=THT]

nets:
  N1: 부품1.D8, LED1.anode
  N2: 부품1.D9_PWM, LED2.anode
  N3: 부품1.D11_PWM/MOSI, LED3.anode
  N4: 부품1.D2, hc-sr1.Trig
  N5: 부품1.D3_PWM, hc-sr1.Echo
  5V: 부품1.5V, hc-sr1.VCC
  GND: 부품1.GND, hc-sr1.GND, R1.Pin_1, R2.Pin_1
  N6: LED1.cathode, R1.Pin_0
  N7: LED2.cathode, R2.Pin_0
  N8: LED3.cathode, R3.Pin_0
