# Fritzing sketch dht11_display (saved by Fritzing 0.9.3b)
breadboards: 1

parts:
  부품1 = Arduino Uno (Rev3)
  R6 = Resistor [tolerance=±5% resistance=220 package=THT]  # not connected
  U2 = LCD-16X2 [package=lcd-16x2_noholes]  # not connected
  R7 = Rotary Potentiometer (Small) [maximum_resistance=100kΩ package=THT]
  R8 = Resistor [tolerance=±5% resistance=220 package=THT]
  Part1 = KY-015 Temperature & Humidity Sensor Module [package="Breakout board"]

nets:
  N1: 부품1.D8, Part1.Vin
  N2: 부품1.GND, R7.leg1, Part1.-
  N3: 부품1.5V, R7.leg2, R8.Pin_1, Part1.S

custom parts:
  KY-015 Temperature & Humidity Sensor Module: KY-015 temperature and humidity sensor module, provides a low-latency serial interface to measure humidity and temperature.
