# Fritzing sketch ga (saved by Fritzing 0.9.3b)
breadboards: 1

parts:
  부품1 = Arduino Uno (Rev3)
  R5 = Rotary Potentiometer (Small) [maximum_resistance=100kΩ package=THT]

nets:
  N1: 부품1.A0, R5.wiper
  N2: 부품1.5V, R5.leg1
  N3: 부품1.GND, R5.leg2
