# Fritzing sketch ga_analogWrite (saved by Fritzing 0.9.3b)
breadboards: 1

parts:
  부품1 = Arduino Uno (Rev3)
  R5 = Rotary Potentiometer (Small) [maximum_resistance=100kΩ package=THT]
  LED1 = LED - 5mm [color="Red (633nm)" package="5 mm [THT]"]
  R6 = Resistor [tolerance=±5% resistance=220 package=THT]

nets:
  N1: 부품1.A0, R5.wiper
  N2: 부품1.D10_PWM/SS, LED1.anode
  N3: 부품1.GND, R5.leg2, R6.Pin_0
  N4: 부품1.5V, R5.leg1
